# Fritzing sketch UTS - Kelompok 2 (saved by Fritzing 0.8.7b)
breadboards: 1

parts:
  LCD2 = LCD screen
  LCM1602_IIC2 = LCM1602 IIC [part_number="LCM1602 IIC" chip_label="LCM1602 IIC" package="DIP (Dual Inline) [THT]"]
  e-radionica_com1 = LM393 LDR breakout [part_number=100027]
  U1 = NodeMCU V3.0
  DHT1 = DHT11 Humitidy and Temperature Sensor
  Part2 = SRF05 Ultrasonic Rangefinder
  LED1 = RGB LED - (4 legs) [package="5 mm [THT]"]
  LED2 = LED - 5mm [color="Yellow (592nm)" package="5 mm [THT]"]

nets:
  VSS: LCD2.VSS, LCM1602_IIC2.VSS
  VDD: LCD2.VDD, LCM1602_IIC2.VDD
  N1: LCD2.V0, LCM1602_IIC2.V0
  N2: LCD2.RS, LCM1602_IIC2.RS
  N3: LCD2.R/W, LCM1602_IIC2.RW
  N4: LCD2.E, LCM1602_IIC2.E
  N5: LCD2.DB0, LCM1602_IIC2.D0
  N6: LCD2.DB1, LCM1602_IIC2.D1
  N7: LCD2.DB2, LCM1602_IIC2.D2
  N8: LCD2.DB3, LCM1602_IIC2.D3
  N9: LCD2.DB4, LCM1602_IIC2.D4
  N10: LCD2.DB5, LCM1602_IIC2.D5
  N11: LCD2.DB6, LCM1602_IIC2.D6
  N12: LCD2.DB7, LCM1602_IIC2.D7
  N13: LCD2.LED+, LCM1602_IIC2.A
  N14: LCD2.LED-, LCM1602_IIC2.K
  GND: LCM1602_IIC2.GND, e-radionica_com1.GND, U1.GND#6, U1.GND#13, U1.GND#16, U1.GND#33, DHT1.GND, Part2.GND, LED1.common_anode, LED2.anode
  VCC: LCM1602_IIC2.VCC, e-radionica_com1.VCC, U1.Vin, Part2.VCC
  N15: LCM1602_IIC2.SDA, U1.D2
  N16: LCM1602_IIC2.SCL, U1.D1
  N17: LCM1602_IIC2.LED_A, LCM1602_IIC2.LED_B
  N18: e-radionica_com1.AO, U1.A0
  N19: U1.D0, LED1.blue_cathode
  N20: U1.D3, LED2.cathode
  N21: U1.D4, LED1.red_cathode
  3V3: U1.3V3, DHT1.VDD
  N22: U1.D5, Part2.Trig
  N23: U1.D6, Part2.Echo
  N24: U1.D7, LED1.green_cathode
  N25: U1.D8, DHT1.DATA

custom parts:
  LCM1602 IIC: I2C-Module to use a 1602 or 2004 LCD on with the wire.h libory Serial LCD Modul
  NodeMCU V3.0: ESP8266 based NodeMCU
  DHT11 Humitidy and Temperature Sensor: DHT11 Humidity and Temperature Sensor
